// Digital circuit Lab00b.dig as structural Verilog
module Lab00b (
);

  wire led1_p2, switch1_b;

  // PolarityAwareLED led1: pin names not known; wires that end beside it: 1'b1, led1_p2
  Switch #(.switchActsAsInput("true")) switch1 (.A(led1_p2), .B(switch1_b));
  Switch #(.switchActsAsInput("true")) switch2 (.A(1'b0), .B(switch1_b));
endmodule
